# Fritzing sketch Schematic_Arduino (saved by Fritzing 0.9.3b)
breadboards: 1

parts:
  Composant1 = Arduino Nano (Rev3.0) [part_number=Arduino]
  R1 = Resistor [tolerance=±5% resistance=150 package=THT]
  LED1 = LED - 3mm [color="Infrared (850nm)" package="3 mm [THT]"]
  S1 = Taiway 100-SP-X-T1 SPDT Miniature Toggle Switch [package=THT]
  S2 = Pushbutton [package="[THT]"]
  C1 = Ceramic Capacitor [capacitance=100nF package="100 mil [THT, multilayer]"]
  R2 = Resistor [tolerance=±5% resistance=10k package=THT]
  U1 = mystery part, 3 pins [chip_label="IR Receiver"]

nets:
  N1: Composant1.GND, LED1.cathode, S1.L1, R2.Pin_1, U1.pin3
  N2: Composant1.D3, R1.Pin_0
  N3: Composant1.D7, S1.COM
  N4: Composant1.D8, U1.pin2
  N5: Composant1.D9, S2.Pin_3, S2.Pin_4, C1.0, R2.Pin_0
  N6: Composant1.5V, S1.L2, S2.Pin_1, S2.Pin_2, C1.1, U1.pin1
  N7: R1.Pin_1, LED1.anode
